# Fritzing sketch Junk (saved by Fritzing 0.9.3b)
breadboards: 1

parts:
  R1 = Resistor [tolerance=±5% resistance=220 package=THT]
  R2 = Resistor [tolerance=±5% resistance=220 package=THT]
  C1 = Ceramic Capacitor [capacitance=100nF package="100 mil [THT, multilayer]"]
  J1 = female pin header, 2 pins [form="♀ (female)"]
  R3 = Resistor [tolerance=±5% resistance=220 package=THT]  # not connected

nets:
  N1: R1.Pin_0, R2.Pin_0
  N2: R1.Pin_1, J1.pin2
  N3: R2.Pin_1, C1.1
  N4: C1.0, J1.pin1
