# Fritzing sketch RotaryEncoderDiagram (saved by Fritzing 0.9.3b)
breadboards: 1

parts:
  R1 = Resistor [tolerance=±5% resistance=10k package=THT]
  R2 = Resistor [tolerance=±5% resistance=10k package=THT]
  R3 = Resistor [tolerance=±5% resistance=10k package=THT]
  R4 = Resistor [tolerance=±5% resistance=10k package=THT]
  R5 = Resistor [tolerance=±5% resistance=10k package=THT]
  R7 = Resistor [tolerance=±5% resistance=10k package=THT]
  J1 = female pin header, 8 pins [form="♀ (female)"]
  C1 = Ceramic Capacitor [capacitance=100nF package="100 mil [THT, multilayer]"]
  C2 = Ceramic Capacitor [capacitance=100nF package="100 mil [THT, multilayer]"]
  J2 = female pin header, 3 pins [form="♀ (female)"]
  J3 = female pin header, 3 pins [form="♀ (female)"]
  J4 = female pin header, 3 pins [form="♀ (female)"]
  J5 = female pin header, 3 pins [form="♀ (female)"]
  C3 = Ceramic Capacitor [capacitance=100nF package="100 mil [THT, multilayer]"]
  C4 = Ceramic Capacitor [capacitance=100nF package="100 mil [THT, multilayer]"]
  R9 = Resistor [tolerance=±5% resistance=10k package=THT]
  R10 = Resistor [tolerance=±5% resistance=10k package=THT]

nets:
  N1: R1.Pin_0, R2.Pin_0, R3.Pin_0, R4.Pin_0, J1.pin5
  N2: R1.Pin_1, R5.Pin_0, J2.pin1
  N3: R2.Pin_1, R7.Pin_0, J2.pin3
  N4: R3.Pin_1, J3.pin3, R10.Pin_1
  N5: R4.Pin_1, J3.pin1, R9.Pin_1
  N6: R5.Pin_1, J1.pin2, C1.1
  N7: R7.Pin_1, J1.pin3, C2.1
  N8: J1.pin1, C1.0, C2.0, J2.pin2, J3.pin2, J4.pin1, J5.pin3, C3.0, C4.0
  N9: J1.pin4, J4.pin3
  N10: J1.pin6, J5.pin1
  N11: J1.pin7, C3.1, R9.Pin_0
  N12: J1.pin8, C4.1, R10.Pin_0
